# Fritzing sketch ╗µ═╝╩╛└²ú¿1602╥║╛ºú⌐ (saved by Fritzing 0.8.7b)
circuit board: 11.5194cm x 13.2271cm
breadboards: 1

parts:
  元件1 = Arduino Uno (Rev3)
  LCD1 = LCD screen
  R1 = Trimmer Potentiometer [maximum_resistance=10kΩ package=THT]

nets:
  N1: 元件1.D8, LCD1.DB1
  N2: 元件1.D9_PWM, LCD1.DB0
  N3: 元件1.D10_PWM/SS, LCD1.E
  N4: 元件1.D11_PWM/MOSI, LCD1.R/W
  N5: 元件1.D12/MISO, LCD1.RS
  GND: 元件1.GND, LCD1.VSS, LCD1.LED-, R1.wiper
  N6: 元件1.D2, LCD1.DB7
  N7: 元件1.D3_PWM, LCD1.DB6
  N8: 元件1.D4, LCD1.DB5
  N9: 元件1.D5_PWM, LCD1.DB4
  N10: 元件1.D6_PWM, LCD1.DB3
  N11: 元件1.D7, LCD1.DB2
  5V: 元件1.5V, LCD1.VDD, LCD1.LED+
  N12: LCD1.V0, R1.leg2
